// Logisim project SomadorCompleto.circ as structural Verilog: 4 circuits, main circuit main
module main (
);

  Meio_Somador meio_somador_1 ();  // open: Soma, Carry_Out, A0, B0
endmodule

module Meio_Somador (
  input  A0,
  input  B0,
  output Soma,
  output Carry_Out
);

  xor xor_1 (Soma, A0, B0);
  and and_1 (Carry_Out, A0, B0);
endmodule

module Somador_Completo__Abstraido (
  input  A,
  input  B,
  input  Ci,
  output Soma,
  output Co
);

  wire meio_somador_1_carry_out, meio_somador_1_soma, meio_somador_2_carry_out;

  Meio_Somador meio_somador_1 (.Soma(meio_somador_1_soma), .Carry_Out(meio_somador_1_carry_out), .A0(A), .B0(B));
  Meio_Somador meio_somador_2 (.Soma(Soma), .Carry_Out(meio_somador_2_carry_out), .A0(meio_somador_1_soma), .B0(Ci));
  or or_1 (Co, meio_somador_2_carry_out, meio_somador_1_carry_out);
endmodule

module Somador_Completo (
  input  Ci,
  input  A0,
  input  B0,
  output Soma,
  output Carry_Out,
  output Carry_Out_2,
  output Soma_2,
  output Carry_Out_3
);

  xor xor_1 (Soma, A0, B0);
  and and_1 (Carry_Out, A0, B0);
  xor xor_2 (Soma_2, Ci, Soma);
  and and_2 (Carry_Out_3, Ci, Soma);
  or or_1 (Carry_Out_2, Carry_Out, Carry_Out_3);
endmodule
